// Digital circuit fsm_5-bit_counter.dig as structural Verilog
module fsm_5_bit_counter (
  input  CLK,
  input  clr,
  output Q4,
  output Q3,
  output Q2,
  output Q1,
  output Q0
);

  wire jk_ff_as_1_nq, jk_ff_as_2_nq, jk_ff_as_3_nq, jk_ff_as_4_nq;

  JK_FF_AS jk_ff_as_1 (.Set(1'b0), .J(1'b1), .C(CLK), .K(1'b1), .Clr(clr), .Q(Q0), .nQ(jk_ff_as_1_nq));
  JK_FF_AS jk_ff_as_2 (.Set(1'b0), .J(1'b1), .C(jk_ff_as_1_nq), .K(1'b1), .Clr(clr), .Q(Q1), .nQ(jk_ff_as_2_nq));
  JK_FF_AS jk_ff_as_3 (.Set(1'b0), .J(1'b1), .C(jk_ff_as_2_nq), .K(1'b1), .Clr(clr), .Q(Q2), .nQ(jk_ff_as_3_nq));
  JK_FF_AS jk_ff_as_4 (.Set(1'b0), .J(1'b1), .C(jk_ff_as_3_nq), .K(1'b1), .Clr(clr), .Q(Q3), .nQ(jk_ff_as_4_nq));
  JK_FF_AS jk_ff_as_5 (.Set(1'b0), .J(1'b1), .C(jk_ff_as_4_nq), .K(1'b1), .Clr(clr), .Q(Q4));  // open: nQ
endmodule
