// Digital circuit fsm_traffic.dig as structural Verilog
module fsm_traffic (
  input  clk,
  input  A
);

  wire and_1_out, and_2_out, fsm_5_bit_counter_1_q0, fsm_5_bit_counter_1_q1, fsm_5_bit_counter_1_q2,
       fsm_5_bit_counter_1_q3, fsm_5_bit_counter_1_q4, nor_1_out, nor_2_out, or_1_out;

  fsm_5_bit_counter fsm_5_bit_counter_1 (
    .clr(A), .CLK(clk), .Q4(fsm_5_bit_counter_1_q4), .Q3(fsm_5_bit_counter_1_q3),
    .Q2(fsm_5_bit_counter_1_q2), .Q1(fsm_5_bit_counter_1_q1), .Q0(fsm_5_bit_counter_1_q0));
  and and_1 (and_1_out, fsm_5_bit_counter_1_q3, fsm_5_bit_counter_1_q2, fsm_5_bit_counter_1_q1, fsm_5_bit_counter_1_q0);
  or or_1 (or_1_out, fsm_5_bit_counter_1_q3, fsm_5_bit_counter_1_q2, fsm_5_bit_counter_1_q1, fsm_5_bit_counter_1_q0);
  nor nor_1 (nor_1_out, fsm_5_bit_counter_1_q4, and_1_out);
  and and_2 (and_2_out, fsm_5_bit_counter_1_q4, or_1_out);
  nor nor_2 (nor_2_out, nor_1_out, and_2_out);
  LED g (.in(nor_1_out));
  LED y (.in(nor_2_out));
  LED r (.in(and_2_out));
endmodule
